# Fritzing sketch ECTE250 (saved by Fritzing 0.9.2b)
breadboards: 1

parts:
  Raspberry_Pi1 = Raspberry Pi 2
  U1 = atmega328 [package=dip]
  Part1 = Gas Sensor Breakout Board
  Y1 = CRYSTAL [package=hc49us]
  R1 = Resistor [tolerance=±5% resistance=10k package="0805 [SMD]"]
  C1 = Ceramic Capacitor [capacitance=22pF package="100 mil [THT, multilayer]"]
  C2 = Ceramic Capacitor [capacitance=22pF package="100 mil [THT, multilayer]"]
  J1 = Piezo Speaker
  Part2 = Gas Sensor Breakout Board
  Nokia_5110_LCD_Module2 = Nokia5110LCDModule
  Q1 = NPN-Transistor [package="SOT-23 [SMD]"]
  T1 = LM35 Temperature Sensor [package="TO92 [THT]"]
  R2 = Resistor [tolerance=±5% resistance=2.2k package="0805 [SMD]"]

nets:
  3V3: Raspberry_Pi1.3v3, Nokia_5110_LCD_Module2.Vcc, Nokia_5110_LCD_Module2.LED
  GND: Raspberry_Pi1.GPIO3, Raspberry_Pi1.GPIO27, Raspberry_Pi1.GPIO10, Raspberry_Pi1.GND, U1.GND, Part1.GND, J1.pin1, Part2.GND, Nokia_5110_LCD_Module2.Grnd, Nokia_5110_LCD_Module2.SCLK, T1.GND
  N1: Raspberry_Pi1.GPIO22, Q1.0
  N2: Raspberry_Pi1.GPIO11, Nokia_5110_LCD_Module2.6_DN_(MOSI)
  N3: Raspberry_Pi1.GPIO8, Nokia_5110_LCD_Module2.D/C
  N4: Raspberry_Pi1.GPIO24, Nokia_5110_LCD_Module2.RST
  N5: Raspberry_Pi1.GPIO23, Nokia_5110_LCD_Module2.SCE
  N6: Raspberry_Pi1.GPIO15, U1.D0_(RX)
  N7: Raspberry_Pi1.GPIO14, U1.D1_(TX)
  5V: Raspberry_Pi1.5V, U1.VCC, U1.AVCC, Part1.A1, Part1.H1, R1.Pin_1, C1.1, C2.0, Part2.H1, Part2.A1, Q1.2, R2.Pin_1
  N8: U1.RESET, R1.Pin_0
  N9: U1.XLAT1, Y1.2, C2.1
  N10: U1.XLAT2, Y1.1, C1.0
  N11: U1.A3, T1.Vout, R2.Pin_0
  N12: U1.A4, Part2.B1
  N13: U1.A5, Part1.B1
  N14: J1.pin2, Q1.1

custom parts:
  : Nokia 5110 LCD with 8 pin. It's a 45mm*45mm module part. Description: The Nokia 5110 is a basic graphic LCD screen for lots of applications. It was originally intended for as a cell phone screen. This one is mounted on an easy to solder PCB. It uses the PCD8544 controller. The PCD8544 is a low power CMOS LCD controller/driver, designed to drive a graphic display of 48 rows and 84 columns. All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
